# Fritzing sketch PredictiveWateringSystem (saved by Fritzing 0.9.9b)
breadboards: 1

parts:
  Argon1 = Particle Argon
  OLED_I2C1 = OLED 128x64 I2C Monochrome Display
  SENS1 = SoilWatch 10
  Part1 = Adafruit MicroSD card breakout board [part_number="Adafruit #254"]
  M1 = BMP280
  Grove1 = Grove Dust Sensor
  Part2 = MQ-131 breakout
  S1 = Pushbutton [package="[THT]"]
  Neopixel1 = Adafruit RBG Smart Neopixel [package="DIP (Dual Inline) [THT]"]
  Water_Level_Sensor1 = Water Level Sensor
  R1 = Resistor [tolerance=±5% power=0.25 resistance=10k package=THT]
  KY-1 = Keyes Relay [package=THT]
  WATER_PUMP1 = water pump/motor  # not connected

nets:
  VCC: Argon1.3.3V, OLED_I2C1.VDD, SENS1.VCC, Part1.+3V3, M1.VIN, Grove1.VCC, Part2.VCC, S1.Pin_1, S1.Pin_2
  GND: Argon1.GND, OLED_I2C1.GND, SENS1.GND, Part1.GND, M1.GND, Grove1.GND, Part2.GND, Neopixel1.G, Water_Level_Sensor1.GND, R1.Pin_1, KY-1.ground
  N1: Argon1.A0, Part2.AO
  N2: Argon1.A1, SENS1.OUT
  N3: Argon1.A2, Water_Level_Sensor1.SIG
  N4: Argon1.A5, Part1.CS
  N5: Argon1.SCK, Part1.CLK
  N6: Argon1.MO, Part1.DI
  N7: Argon1.MI, Part1.DO
  N8: Argon1.SDA, OLED_I2C1.SDA, M1.SDA
  N9: Argon1.SCL, OLED_I2C1.SCK, M1.SCL
  N10: Argon1.D3, Grove1.SIG
  N11: Argon1.D4, S1.Pin_3, S1.Pin_4, R1.Pin_0
  N12: Argon1.D5, Neopixel1.In
  N13: Argon1.D6, Water_Level_Sensor1.VCC
  N14: Argon1.D8, KY-1.power
  N15: Argon1.VUSB, Neopixel1.+, KY-1.signal
  N16: KY-1.NC, KY-1.C, KY-1.NO

custom parts:
  Particle Argon: The Argon is a powerful Wi-Fi enabled development board that can act as either a standalone Wi-Fi endpoint or Wi-Fi enabled gateway for Particle Mesh networks. It is based on the Nordic nRF52840 and has built-in battery charging circuitry so it’s easy to connect a Li-Po and deploy your local network in minutes. The Argon is great for connecting existing projects to the Particle Device Cloud or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
  SoilWatch 10: SoilWatch 10 - Capacitive soil moisture sensor
  Adafruit MicroSD card breakout board: Not just a simple breakout board, this microSD adapter goes the extra mile - designed for ease of use. Onboard 5v->3v regulator provides 150mA for power-hungry cards 3v level shifting means you can use this with ease on either 3v or 5v systems Uses a proper level shifting chip, not resistors: less problems, and faster read/write access Use 3 or 4 digital pins to read and write 2Gb+ of storage!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
  BMP280: Temperature Humidity Barometric presure Sensor, I2C
  Grove Dust Sensor: PPD42 Grove Dust Sensor
  MQ-131 breakout: SKU: 101282
  Pushbutton: A generic pushbutton.
  Water Level Sensor: A water level sensor. This sensor operates at 3V to 5V. The Sig (signal) pin outputs an analogue signal that is in proportion to the amount of water in contact with the sensor.
  Keyes Relay: The Keyes 5V relay module is suitable for SCM development, home appliance control. It uses a 5V~12V TIL control signal which can control DC / AC signal.
  water pump/motor: WATER PUMP BY ARDUBLOCKTR
